# Fritzing sketch Circuits and Systems Design - Final Fritzing (saved by Fritzing 1.0.2b)
perfboards: 2

parts:
  esp1 = ESP32 DevKitc V4
  YwRobot_Power_Supply1 = YwRobot Breadboard Power Supply [part_number=545043]  # not connected
  VCC1 = Battery block 9V [internal_resistance=0.1Ω]  # not connected
  Part3 = InvenSense MPU6050
  RotationSensorDFR2 = RotationSensorDFR0058
  CUI-enc4 = AMT103
  A2 = Keyestudio Ks0272
  USBTTL3 = Micro USB B Plug  # not connected
  S1 = Pushbutton [package="[THT]"]
  S2 = Pushbutton [package="[THT]"]

nets:
  N1: esp1.IO15, RotationSensorDFR2.GND
  N2: esp1.IO4, A2.Pin_3
  N3: esp1.GND#12, Part3.GND
  N4: esp1.IO22, Part3.SCL
  N5: esp1.GND#18, Part3.AD0
  3V3: esp1.3V3, Part3.VCC
  N6: esp1.IO32, S1.Pin_3, S1.Pin_4
  N7: esp1.IO33, S2.Pin_3, S2.Pin_4
  N8: esp1.IO25, CUI-enc4.X
  N9: esp1.IO26, CUI-enc4.A
  N10: esp1.IO27, CUI-enc4.5V
  N11: esp1.IO14, CUI-enc4.B
  N12: esp1.GND#32, CUI-enc4.GND
  N13: S1.Pin_1, S1.Pin_2, S2.Pin_1, S2.Pin_2

notes:
  Circuit Wiring for Common Source Amplifier, Circuit Wiring for Common Source Amplifier

custom parts:
  ESP32 DevKitc V4: ESP32-DevKitC board with ESP32-WROOM-32 module. ESP32-DevKitC V4 is a small-sized ESP32-based development board produced by Espressif. Most of the pins on the ESP module are broken out to the pin headers on the board. The pins D0, D1, D2, D3, CMD and CLK are used internally for communication between ESP32 and SPI flash memory. They are grouped on both sides near the USB connector. Avoid using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
  YwRobot Breadboard Power Supply: The YwRobot Breadboard Power Supply (MB-V2) has two power rails; they can be 5V or 3V3. Power to the module can be provided through the female USB socket or through the A10 (female) 2.1mm power jack.
  AMT103: CUI AMT103 Modular incremental encoder. Resolutions 48, 96, 100, 125, 192, 200, 250, 256, 384, 400, 500, 512, 800, 1000, 1024, 2048 either fixed (resolution indicated by part number) or selectable via dip switch. Index output once per revolution. VCC 5V (3.6V min, probably too high for 3.3V operation)
  Keyestudio Ks0272: This vibration sensor is based on piezoelectric ceramic chip analog vibration. It makes use of the anti-conversion process that piezoelectric ceramic vibration will generate the electric signals.
