# Fritzing sketch Circuits and Systems Design - Floating Mouse Recovery (saved by Fritzing 1.0.6)
breadboards: 4

parts:
  esp1 = ESP32 DevKitc V4  # not connected
  S2 = Pushbutton [package="[THT]"]
  Part1 = Adafruit ADXL345 [part_number="Adafruit #1231"]
  R1 = Resistor [tolerance=±5% resistance=100k package="0805 [SMD]"]
  R2 = Resistor [tolerance=±5% resistance=1k package="0805 [SMD]"]
  S3 = Pushbutton [package="[THT]"]
  R3 = Resistor [tolerance=±5% resistance=100k package="0805 [SMD]"]
  C1 = Electrolytic Capacitor [capacitance=4.7nF voltage=35V package="0807 [SMD, electrolytic]"]
  R5 = Resistor [tolerance=±5% resistance=1k package="0805 [SMD]"]
  C2 = Electrolytic Capacitor [capacitance=4.7nF voltage=35V package="0807 [SMD, electrolytic]"]
  RotationSensorDFR1 = RotationSensorDFR0058
  YwRobot_Power_Supply1 = YwRobot Breadboard Power Supply [part_number=545043]  # not connected
  VCC1 = Battery block 9V [internal_resistance=0.1Ω]  # not connected
  M1 = bb-usb-cable [package=THT]  # not connected
  A1 = Keyestudio Ks0272
  CUI-enc3 = AMT103

nets:
  N1: S2.Pin_1, S2.Pin_2, R1.Pin_0, R2.Pin_1
  N2: S2.Pin_3, C1.+, A1.Pin_1
  N3: Part1.VIN, R3.Pin_0, RotationSensorDFR1.SIGNAL
  GND: Part1.GND, CUI-enc3.GND
  N4: R2.Pin_0, C1.-
  N5: S3.Pin_2, R3.Pin_1, R5.Pin_1
  N6: S3.Pin_3, S3.Pin_4, C2.-
  N7: R5.Pin_0, C2.+

notes:
  Circuit Wiring for Common Source Amplifier, Circuit Wiring for Common Source Amplifier

custom parts:
  ESP32 DevKitc V4: ESP32-DevKitC board with ESP32-WROOM-32 module. ESP32-DevKitC V4 is a small-sized ESP32-based development board produced by Espressif. Most of the pins on the ESP module are broken out to the pin headers on the board. The pins D0, D1, D2, D3, CMD and CLK are used internally for communication between ESP32 and SPI flash memory. They are grouped on both sides near the USB connector. Avoid using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
  Adafruit ADXL345: Filling out our accelerometer offerings, we now have the really lovely digital ADXL345 from Analog Devices, a triple-axis accelerometer with digital I2C and SPI interface breakout. We added an on-board 3.3V regulator and logic-level shifting circuitry, making it a perfect choice for interfacing with any 3V or 5V microcontroller such as the Arduino. The sensor has three axes of measurements, X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
  YwRobot Breadboard Power Supply: The YwRobot Breadboard Power Supply (MB-V2) has two power rails; they can be 5V or 3V3. Power to the module can be provided through the female USB socket or through the A10 (female) 2.1mm power jack.
  bb-usb-cable: Breadboard only, no connectors USB cable for the Raspberry PIs.
  Keyestudio Ks0272: This vibration sensor is based on piezoelectric ceramic chip analog vibration. It makes use of the anti-conversion process that piezoelectric ceramic vibration will generate the electric signals.
  AMT103: CUI AMT103 Modular incremental encoder. Resolutions 48, 96, 100, 125, 192, 200, 250, 256, 384, 400, 500, 512, 800, 1000, 1024, 2048 either fixed (resolution indicated by part number) or selectable via dip switch. Index output once per revolution. VCC 5V (3.6V min, probably too high for 3.3V operation)
